# Fritzing sketch brazo (saved by Fritzing 0.9.3b)
breadboards: 1

parts:
  Componente1 = Arduino Uno (Rev3)
  J1 = Basic Servo
  J2 = Basic Servo
  J3 = Basic Servo
  M1 = Stepper Motor - Unipolar
  IC1 = L293D [package=THT]
  VCC1 = Battery  # not connected

nets:
  N1: Componente1.D8, Componente1.D9_PWM, Componente1.D10_PWM/SS, Componente1.D11_PWM/MOSI, M1.B, M1.COMMON_2, M1.D, IC1.Enable_1, IC1.In_1, IC1.Out_1_(_Controlled_by_Enable_1_), IC1.0V, IC1.Out_4_(_Controlled_by_Enable_2_), IC1.In_4, IC1.+V
  GND: Componente1.GND, J1.gnd, J2.gnd, IC1.Out_3_(_Controlled_by_Enable_2_)
  N2: Componente1.D2, J3.pulse
  N3: Componente1.D3_PWM, J2.pulse
  N4: Componente1.D4, J1.pulse
  VCC: Componente1.5V, J1.vcc, J2.vcc, J3.vcc, IC1.Out_2_(_Controlled_by_Enable_1_)
  N5: IC1.In_2, IC1.+Vmotor
  N6: IC1.Enable_2, IC1.In_3
